// Logisim project DeMultiplexer.circ as structural Verilog: 1 circuit, main circuit main
module main (
  input  A,
  input  B,
  input  Fixed_D,
  output out_4,
  output out_5,
  output out_6,
  output out_7
);

  wire not_1_out, not_2_out;

  not not_1 (not_1_out, A);
  not not_2 (not_2_out, B);
  and and_1 (out_4, Fixed_D, not_2_out, not_1_out);
  and and_2 (out_5, Fixed_D, not_2_out, A);
  and and_3 (out_6, Fixed_D, B, not_1_out);
  and and_4 (out_7, Fixed_D, B, A);

  // Notes on the sheet:
  //   DeMultiplexer
endmodule
