// Logisim project Full subtractor.circ as structural Verilog: 1 circuit, main circuit main
module main (
  input  A,
  input  B,
  input  Borrow_in,
  output Differ,
  output Borrow_Out
);

  wire and_1_out, and_2_out, not_1_out, not_2_out, undriven, xor_1_out;

  xor xor_1 (xor_1_out, A, B);
  not not_1 (not_1_out, A);
  not not_2 (not_2_out, xor_1_out);
  and and_1 (and_1_out, not_1_out, B);
  and and_2 (and_2_out, not_2_out, Borrow_in);
  xor xor_2 (Differ, xor_1_out, Borrow_in);
  or or_1 (Borrow_Out, and_2_out, undriven, and_1_out);

  // Notes on the sheet:
  //   Full Subtractor
endmodule
