// Logisim project Half Subtractor.circ as structural Verilog: 1 circuit, main circuit main
module main (
  input  A,
  input  B,
  output Difference,
  output Borrow
);

  wire and_1_out, and_2_out, not_1_out, not_2_out, not_3_out;

  not not_1 (not_1_out, B);
  not not_2 (not_2_out, A);
  and and_1 (and_1_out, A, not_1_out);
  and and_2 (and_2_out, not_2_out, B);
  not not_3 (not_3_out, A);
  or or_1 (Difference, and_1_out, and_1_out, and_2_out, and_2_out);
  and and_3 (Borrow, not_3_out, B);

  // Notes on the sheet:
  //   Half Subtractor
endmodule
