// Logisim project Multiplexer.circ as structural Verilog: 1 circuit, main circuit main
module main (
  input  A,
  input  Sum,
  input  B,
  output out_4
);

  wire and_1_out, and_2_out, not_1_out;

  not not_1 (not_1_out, Sum);
  and and_1 (and_1_out, A, Sum);
  and and_2 (and_2_out, B, not_1_out);
  or or_1 (out_4, and_1_out, and_2_out);

  // Notes on the sheet:
  //   Multiplexer
endmodule
