// Logisim project NAND,NOR,XOR.circ as structural Verilog: 1 circuit, main circuit main
module main (
  input  in_1,
  input  in_2,
  input  in_3,
  input  in_4,
  input  in_5,
  input  in_6,
  output NAND,
  output NOR,
  output XOR
);

  wire and_1_out, and_2_out, and_3_out, not_1_out, not_2_out, or_1_out;

  not not_1 (not_1_out, in_6);
  not not_2 (not_2_out, in_5);
  and and_1 (and_1_out, in_5, not_1_out);
  and and_2 (and_2_out, not_2_out, in_6);
  and and_3 (and_3_out, in_1, in_2, in_2);
  or or_1 (or_1_out, in_3, in_4, in_4);
  or or_2 (XOR, and_1_out, and_1_out, and_2_out, and_2_out);
  not not_3 (NAND, and_3_out);
  not not_4 (NOR, or_1_out);

  // Notes on the sheet:
  //   NAND , NOR, XOR
endmodule
