// Logisim project SR & D flip flop.circ as structural Verilog: 1 circuit, main circuit main
module main (
  input  S,
  input  R,
  input  D,
  output Q,
  output Q_prime,
  output Q_2,
  output Q_prime_2
);

  wire and_1_out, and_2_out, and_3_out, and_4_out, clock_1_out, clock_2_out, not_1_out, or_1_out, or_2_out,
       or_3_out, or_4_out;

  Clock clock_1 (.out(clock_1_out));
  Clock clock_2 (.out(clock_2_out));
  not not_1 (not_1_out, D);
  and and_1 (and_1_out, S, clock_2_out);
  and and_2 (and_2_out, R, clock_2_out);
  and and_3 (and_3_out, not_1_out, clock_1_out);
  and and_4 (and_4_out, D, clock_1_out);
  or or_1 (or_1_out, and_1_out, Q_prime);
  or or_2 (or_2_out, Q, and_2_out);
  or or_3 (or_3_out, and_3_out, Q_prime_2);
  not not_2 (Q_2, or_3_out);
  or or_4 (or_4_out, Q_2, and_4_out);
  not not_3 (Q_prime_2, or_4_out);
  not not_4 (Q, or_1_out);
  not not_5 (Q_prime, or_2_out);

  // Notes on the sheet:
  //   SR Flip Flop
  //   D Flip Flop
endmodule
